# Fritzing sketch esquema.fzzes (saved by Fritzing 0.9.3b)
breadboards: 1

parts:
  Componente1 = Arduino Leonardo (Rev3b)
  S1 = Pushbutton [package="[THT]"]
  LED1 = LED - 5mm [color="Red (633nm)" package="5 mm [THT]"]
  R1 = Resistor [tolerance=±5% resistance=330k package=THT]
  S2 = Pushbutton [package="[THT]"]
  S3 = Pushbutton [package="[THT]"]
  S4 = Pushbutton [package="[THT]"]
  S5 = Pushbutton [package="[THT]"]

nets:
  N1: Componente1.D3_PWM/SCL, LED1.anode
  N2: Componente1.D5_PWM, S4.Pin_3, S4.Pin_4
  N3: Componente1.D6_PWM/A7, S5.Pin_3, S5.Pin_4
  N4: Componente1.D8/A8, S3.Pin_3, S3.Pin_4
  N5: Componente1.D9_PWM/A9, S2.Pin_3, S2.Pin_4
  N6: Componente1.D10_PWM/A10, Componente1.GND, S1.Pin_3, S1.Pin_4, R1.Pin_0, S2.Pin_1, S2.Pin_2, S3.Pin_1, S3.Pin_2, S4.Pin_1, S4.Pin_2, S5.Pin_1, S5.Pin_2
  N7: S1.Pin_1, S1.Pin_2
  N8: LED1.cathode, R1.Pin_1

notes:
  #define pinLed 3 //led, marron
  //Para el volumen
  #define btnVUp 5 //Vol UP, naranja
  #define btnVDown 6 //Vol Down, amarillo
  //Para ZOOM
  #define btnAudio 8 //Audio, verde
  #define btnVideo 9 //Video, ocre
  #define btnHand 10 //rise hand, morado
